// Logisim project sixteen.circ as structural Verilog
// SPACE
module Computer (
);

  wire _0_out, _1_out, _2_out, _3_out, _4_out, _5_out, _6_out, _7_out, _8_out, _9_out, A_out, B_out,
       button_1_out, button_2_out, button_3_out, button_4_out, button_5_out, button_6_out, button_7_out,
       button_8_out, button_9_out, button_10_out, button_11_out, button_12_out, C_out, cpu_1_wr, D_out,
       E_out, ENTER_out, F_out, G_out, H_out, I_out, J_out, K_out, L_out, M_out, N_out, O_out, P_out, Q_out,
       R_out, S_out, SPACE_out, T_out, U_out, V_out, W_out, X_out, Y_out, Z_out;
  wire [15:0] buffer_5_out, cpu_1_adr, cpu_1_do, mem_1_do;
  wire [31:0] undriven, undriven_2, undriven_3, undriven_4, undriven_5, undriven_6, undriven_7, undriven_8,
       undriven_9, undriven_10, undriven_11, undriven_12, undriven_13, undriven_14, undriven_15, undriven_16,
       undriven_17, undriven_18, undriven_19, undriven_20, undriven_21, undriven_22, undriven_23,
       undriven_24, undriven_25, undriven_26, undriven_27, undriven_28, undriven_29, undriven_30,
       undriven_31, undriven_32, undriven_33, undriven_34, undriven_35, undriven_36, undriven_37,
       undriven_38, undriven_39, undriven_40, undriven_41, undriven_42, undriven_43, undriven_44,
       undriven_45, undriven_46, undriven_47, undriven_48, undriven_49, undriven_50, undriven_51,
       undriven_52, undriven_53, undriven_54, undriven_55, undriven_56, undriven_57, undriven_58,
       undriven_59, undriven_60, undriven_61, undriven_62, undriven_63, undriven_64, undriven_65,
       undriven_66, undriven_67, undriven_68, undriven_69, undriven_70, undriven_71, undriven_72,
       undriven_73, undriven_74, undriven_75, undriven_76, undriven_77, undriven_78, undriven_79,
       undriven_80, undriven_81, undriven_82, undriven_83, undriven_84, undriven_85, undriven_86,
       undriven_87, undriven_88, undriven_89, undriven_90, undriven_91, undriven_92, undriven_93,
       undriven_94, undriven_95, undriven_96, undriven_97, undriven_98, undriven_99, undriven_100,
       undriven_101, undriven_102, undriven_103, undriven_104, undriven_105, undriven_106, undriven_107,
       undriven_108, undriven_109, undriven_110, undriven_111, undriven_112, undriven_113, undriven_114,
       undriven_115, undriven_116, undriven_117, undriven_118, undriven_119, undriven_120, undriven_121,
       undriven_122, undriven_123, undriven_124, undriven_125, undriven_126, undriven_127, undriven_128,
       undriven_129, undriven_130, undriven_131, undriven_132, undriven_133, undriven_134, undriven_135,
       undriven_136, undriven_137, undriven_138, undriven_139, undriven_140, undriven_141, undriven_142,
       undriven_143, undriven_144, undriven_145, undriven_146, undriven_147, undriven_148, undriven_149,
       undriven_150, undriven_151, undriven_152, undriven_153, undriven_154, undriven_155, undriven_156,
       undriven_157, undriven_158, undriven_159, undriven_160, undriven_161, undriven_162, undriven_163,
       undriven_164, undriven_165, undriven_166, undriven_167, undriven_168, undriven_169, undriven_170,
       undriven_171, undriven_172, undriven_173, undriven_174, undriven_175, undriven_176, undriven_177,
       undriven_178, undriven_179, undriven_180, undriven_181, undriven_182, undriven_183, undriven_184,
       undriven_185, undriven_186, undriven_187, undriven_188, undriven_189, undriven_190, undriven_191,
       undriven_192, undriven_193, undriven_194, undriven_195, undriven_196, undriven_197, undriven_198,
       undriven_199, undriven_200, undriven_201, undriven_202, undriven_203, undriven_204, undriven_205,
       undriven_206, undriven_207, undriven_208, undriven_209, undriven_210, undriven_211, undriven_212,
       undriven_213, undriven_214, undriven_215, undriven_216, undriven_217, undriven_218, undriven_219,
       undriven_220, undriven_221, undriven_222, undriven_223, undriven_224, undriven_225, undriven_226,
       undriven_227, undriven_228, undriven_229, undriven_230, undriven_231, undriven_232, undriven_233,
       undriven_234, undriven_235, undriven_236, undriven_237, undriven_238, undriven_239, undriven_240,
       undriven_241, undriven_242, undriven_243, undriven_244, undriven_245, undriven_246, undriven_247,
       undriven_248, undriven_249, undriven_250, undriven_251, undriven_252, undriven_253, undriven_254,
       undriven_255, undriven_256;

  DotMatrix #(.matrixcols(32), .matrixrows(32)) dotmatrix_1 (
    .col0(undriven), .col1(undriven_3), .col2(undriven_5), .col3(undriven_7), .col4(undriven_9),
    .col5(undriven_11), .col6(undriven_13), .col7(undriven_15), .col8(undriven_17), .col9(undriven_19),
    .col10(undriven_21), .col11(undriven_23), .col12(undriven_25), .col13(undriven_27), .col14(undriven_29),
    .col15(undriven_31), .col16(undriven_33), .col17(undriven_35), .col18(undriven_37), .col19(undriven_39),
    .col20(undriven_41), .col21(undriven_43), .col22(undriven_45), .col23(undriven_47), .col24(undriven_49),
    .col25(undriven_51), .col26(undriven_53), .col27(undriven_55), .col28(undriven_57), .col29(undriven_59),
    .col30(undriven_61), .col31(undriven_63));
  DotMatrix #(.matrixcols(32), .matrixrows(32)) dotmatrix_2 (
    .col0(undriven_2), .col1(undriven_4), .col2(undriven_6), .col3(undriven_8), .col4(undriven_10),
    .col5(undriven_12), .col6(undriven_14), .col7(undriven_16), .col8(undriven_18), .col9(undriven_20),
    .col10(undriven_22), .col11(undriven_24), .col12(undriven_26), .col13(undriven_28), .col14(undriven_30),
    .col15(undriven_32), .col16(undriven_34), .col17(undriven_36), .col18(undriven_38), .col19(undriven_40),
    .col20(undriven_42), .col21(undriven_44), .col22(undriven_46), .col23(undriven_48), .col24(undriven_50),
    .col25(undriven_52), .col26(undriven_54), .col27(undriven_56), .col28(undriven_58), .col29(undriven_60),
    .col30(undriven_62), .col31(undriven_64));
  Button button_1 (.out(button_1_out));
  buf buffer_1 (buffer_5_out[12], button_1_out);
  Button Q (.out(Q_out));
  buf buffer_2 (buffer_5_out[13], Q_out);
  Button A (.out(A_out));
  buf A_2 (buffer_5_out[14], A_out);
  Button Z (.out(Z_out));
  buf buffer_3 (buffer_5_out[15], Z_out);
  Button _2 (.out(_2_out));
  buf buffer_4 (buffer_5_out[1], _1_out);
  Button _1 (.out(_1_out));
  buf buffer_5 (buffer_5_out[0], button_1_out);
  buf buffer_6 (buffer_5_out[12], _1_out);
  buf buffer_7 (buffer_5_out[12], _2_out);
  Button F (.out(F_out));
  Button W (.out(W_out));
  buf buffer_8 (buffer_5_out[1], W_out);
  buf buffer_9 (buffer_5_out[0], Q_out);
  buf buffer_10 (buffer_5_out[13], W_out);
  buf buffer_11 (buffer_5_out[13], F_out);
  buf buffer_12 (buffer_5_out[1], R_out);
  Button S (.out(S_out));
  buf buffer_13 (buffer_5_out[0], A_out);
  Button R (.out(R_out));
  buf buffer_14 (buffer_5_out[14], R_out);
  buf buffer_15 (buffer_5_out[14], S_out);
  Button X (.out(X_out));
  buf buffer_16 (buffer_5_out[0], Z_out);
  buf buffer_17 (buffer_5_out[1], X_out);
  Button C (.out(C_out));
  buf buffer_18 (buffer_5_out[15], X_out);
  buf buffer_19 (buffer_5_out[15], C_out);
  Button _4 (.out(_4_out));
  buf buffer_20 (buffer_5_out[3], _3_out);
  Button _3 (.out(_3_out));
  buf buffer_21 (buffer_5_out[2], _2_out);
  buf buffer_22 (buffer_5_out[12], _3_out);
  buf buffer_23 (buffer_5_out[12], _4_out);
  Button P (.out(P_out));
  buf buffer_24 (buffer_5_out[2], F_out);
  Button G (.out(G_out));
  buf buffer_25 (buffer_5_out[3], P_out);
  buf buffer_26 (buffer_5_out[13], P_out);
  buf buffer_27 (buffer_5_out[13], G_out);
  Button D (.out(D_out));
  buf buffer_28 (buffer_5_out[3], T_out);
  buf buffer_29 (buffer_5_out[2], S_out);
  Button T (.out(T_out));
  buf buffer_30 (buffer_5_out[14], D_out);
  buf buffer_31 (buffer_5_out[14], T_out);
  Button V (.out(V_out));
  buf buffer_32 (buffer_5_out[2], C_out);
  Button B (.out(B_out));
  buf buffer_33 (buffer_5_out[3], V_out);
  buf buffer_34 (buffer_5_out[15], V_out);
  buf buffer_35 (buffer_5_out[15], B_out);
  Screen_Control screen_control_1 (
    .in_1(undriven), .in_2(undriven_3), .in_3(undriven_5), .in_4(undriven_7), .in_5(undriven_9),
    .in_6(undriven_11), .in_7(undriven_13), .in_8(undriven_15), .in_9(undriven_17), .in_10(undriven_19),
    .in_11(undriven_21), .in_12(undriven_23), .in_13(undriven_25), .in_14(undriven_27), .in_15(undriven_29),
    .in_16(undriven_31), .in_17(undriven_33), .in_18(undriven_35), .in_19(undriven_37), .in_20(undriven_39),
    .in_21(undriven_41), .in_22(undriven_43), .in_23(undriven_45), .in_24(undriven_47), .in_25(undriven_49),
    .in_26(undriven_51), .in_27(undriven_53), .in_28(undriven_55), .in_29(undriven_57), .in_30(undriven_59),
    .in_31(undriven_61), .in_32(undriven_63));  // open: sel, addr, data
  Screen_Control screen_control_2 (
    .in_1(undriven_2), .in_2(undriven_4), .in_3(undriven_6), .in_4(undriven_8), .in_5(undriven_10),
    .in_6(undriven_12), .in_7(undriven_14), .in_8(undriven_16), .in_9(undriven_18), .in_10(undriven_20),
    .in_11(undriven_22), .in_12(undriven_24), .in_13(undriven_26), .in_14(undriven_28), .in_15(undriven_30),
    .in_16(undriven_32), .in_17(undriven_34), .in_18(undriven_36), .in_19(undriven_38), .in_20(undriven_40),
    .in_21(undriven_42), .in_22(undriven_44), .in_23(undriven_46), .in_24(undriven_48), .in_25(undriven_50),
    .in_26(undriven_52), .in_27(undriven_54), .in_28(undriven_56), .in_29(undriven_58), .in_30(undriven_60),
    .in_31(undriven_62), .in_32(undriven_64));  // open: sel, addr, data
  Button _5 (.out(_5_out));
  buf buffer_36 (buffer_5_out[4], _4_out);
  Button _6 (.out(_6_out));
  buf buffer_37 (buffer_5_out[5], _5_out);
  buf buffer_38 (buffer_5_out[12], _5_out);
  buf buffer_39 (buffer_5_out[12], _6_out);
  buf buffer_40 (buffer_5_out[5], J_out);
  Button J (.out(J_out));
  Button L (.out(L_out));
  buf buffer_41 (buffer_5_out[4], G_out);
  buf buffer_42 (buffer_5_out[13], L_out);
  buf buffer_43 (buffer_5_out[13], J_out);
  buf buffer_44 (buffer_5_out[4], D_out);
  Button N (.out(N_out));
  Button H (.out(H_out));
  buf buffer_45 (buffer_5_out[5], H_out);
  buf buffer_46 (buffer_5_out[14], H_out);
  buf buffer_47 (buffer_5_out[14], N_out);
  Button K (.out(K_out));
  Button M (.out(M_out));
  buf buffer_48 (buffer_5_out[4], B_out);
  buf buffer_49 (buffer_5_out[5], K_out);
  buf buffer_50 (buffer_5_out[15], M_out);
  buf buffer_51 (buffer_5_out[15], K_out);
  buf buffer_52 (buffer_5_out[4], SPACE_out);
  Button SPACE (.out(SPACE_out));
  DotMatrix #(.matrixcols(32), .matrixrows(32)) dotmatrix_3 (
    .col0(undriven_65), .col1(undriven_67), .col2(undriven_69), .col3(undriven_71), .col4(undriven_73),
    .col5(undriven_75), .col6(undriven_77), .col7(undriven_79), .col8(undriven_81), .col9(undriven_83),
    .col10(undriven_85), .col11(undriven_87), .col12(undriven_89), .col13(undriven_91), .col14(undriven_93),
    .col15(undriven_95), .col16(undriven_97), .col17(undriven_99), .col18(undriven_101),
    .col19(undriven_103), .col20(undriven_105), .col21(undriven_107), .col22(undriven_109),
    .col23(undriven_111), .col24(undriven_113), .col25(undriven_115), .col26(undriven_117),
    .col27(undriven_119), .col28(undriven_121), .col29(undriven_123), .col30(undriven_125),
    .col31(undriven_127));
  DotMatrix #(.matrixcols(32), .matrixrows(32)) dotmatrix_4 (
    .col0(undriven_66), .col1(undriven_68), .col2(undriven_70), .col3(undriven_72), .col4(undriven_74),
    .col5(undriven_76), .col6(undriven_78), .col7(undriven_80), .col8(undriven_82), .col9(undriven_84),
    .col10(undriven_86), .col11(undriven_88), .col12(undriven_90), .col13(undriven_92), .col14(undriven_94),
    .col15(undriven_96), .col16(undriven_98), .col17(undriven_100), .col18(undriven_102),
    .col19(undriven_104), .col20(undriven_106), .col21(undriven_108), .col22(undriven_110),
    .col23(undriven_112), .col24(undriven_114), .col25(undriven_116), .col26(undriven_118),
    .col27(undriven_120), .col28(undriven_122), .col29(undriven_124), .col30(undriven_126),
    .col31(undriven_128));
  Button _7 (.out(_7_out));
  buf buffer_53 (buffer_5_out[6], _6_out);
  Button _8 (.out(_8_out));
  buf buffer_54 (buffer_5_out[7], _7_out);
  buf buffer_55 (buffer_5_out[12], _8_out);
  buf buffer_56 (buffer_5_out[12], _7_out);
  buf buffer_57 (buffer_5_out[6], L_out);
  Button U (.out(U_out));
  buf buffer_58 (buffer_5_out[7], U_out);
  Button Y (.out(Y_out));
  buf buffer_59 (buffer_5_out[13], Y_out);
  buf buffer_60 (buffer_5_out[13], U_out);
  buf buffer_61 (buffer_5_out[6], N_out);
  Button E (.out(E_out));
  Button I (.out(I_out));
  buf buffer_62 (buffer_5_out[7], E_out);
  buf buffer_63 (buffer_5_out[14], I_out);
  buf buffer_64 (buffer_5_out[14], E_out);
  Button button_2 (.out(button_2_out));
  buf buffer_65 (buffer_5_out[7], button_3_out);
  buf buffer_66 (buffer_5_out[6], M_out);
  Button button_3 (.out(button_3_out));
  buf buffer_67 (buffer_5_out[15], button_3_out);
  buf buffer_68 (buffer_5_out[15], button_2_out);
  buf buffer_69 (buffer_5_out[6], SPACE_out);
  buf buffer_70 (buffer_5_out[7], button_9_out);
  Button _0 (.out(_0_out));
  buf buffer_71 (buffer_5_out[8], _8_out);
  buf buffer_72 (buffer_5_out[9], _9_out);
  Button _9 (.out(_9_out));
  buf buffer_73 (buffer_5_out[12], _9_out);
  buf buffer_74 (buffer_5_out[12], _0_out);
  buf buffer_75 (buffer_5_out[8], Y_out);
  buf buffer_76 (buffer_5_out[9], button_5_out);
  Button button_4 (.out(button_4_out));
  Button button_5 (.out(button_5_out));
  buf buffer_77 (buffer_5_out[13], button_5_out);
  buf buffer_78 (buffer_5_out[13], button_4_out);
  buf buffer_79 (buffer_5_out[8], I_out);
  buf buffer_80 (buffer_5_out[9], O_out);
  Button O (.out(O_out));
  Button button_6 (.out(button_6_out));
  buf buffer_81 (buffer_5_out[14], O_out);
  buf buffer_82 (buffer_5_out[14], button_6_out);
  Button button_7 (.out(button_7_out));
  buf buffer_83 (buffer_5_out[8], button_2_out);
  Button button_8 (.out(button_8_out));
  buf buffer_84 (buffer_5_out[9], button_7_out);
  buf buffer_85 (buffer_5_out[15], button_8_out);
  buf buffer_86 (buffer_5_out[15], button_7_out);
  buf buffer_87 (buffer_5_out[9], button_9_out);
  Button button_9 (.out(button_9_out));
  buf buffer_88 (buffer_5_out[11], button_10_out);
  Button button_10 (.out(button_10_out));
  buf buffer_89 (buffer_5_out[10], _0_out);
  buf buffer_90 (buffer_5_out[12], button_10_out);
  buf buffer_91 (buffer_5_out[11], button_11_out);
  Button button_11 (.out(button_11_out));
  buf buffer_92 (buffer_5_out[10], button_4_out);
  buf buffer_93 (buffer_5_out[13], button_11_out);
  Button ENTER (.out(ENTER_out));
  buf buffer_94 (buffer_5_out[11], ENTER_out);
  buf buffer_95 (buffer_5_out[10], button_6_out);
  buf buffer_96 (buffer_5_out[14], ENTER_out);
  buf buffer_97 (buffer_5_out[10], button_8_out);
  buf buffer_98 (buffer_5_out[11], button_12_out);
  Button button_12 (.out(button_12_out));
  buf buffer_99 (buffer_5_out[15], button_12_out);
  Screen_Control screen_control_3 (
    .in_1(undriven_65), .in_2(undriven_67), .in_3(undriven_69), .in_4(undriven_71), .in_5(undriven_73),
    .in_6(undriven_75), .in_7(undriven_77), .in_8(undriven_79), .in_9(undriven_81), .in_10(undriven_83),
    .in_11(undriven_85), .in_12(undriven_87), .in_13(undriven_89), .in_14(undriven_91), .in_15(undriven_93),
    .in_16(undriven_95), .in_17(undriven_97), .in_18(undriven_99), .in_19(undriven_101),
    .in_20(undriven_103), .in_21(undriven_105), .in_22(undriven_107), .in_23(undriven_109),
    .in_24(undriven_111), .in_25(undriven_113), .in_26(undriven_115), .in_27(undriven_117),
    .in_28(undriven_119), .in_29(undriven_121), .in_30(undriven_123), .in_31(undriven_125),
    .in_32(undriven_127));  // open: sel, addr, data
  Screen_Control screen_control_4 (
    .in_1(undriven_66), .in_2(undriven_68), .in_3(undriven_70), .in_4(undriven_72), .in_5(undriven_74),
    .in_6(undriven_76), .in_7(undriven_78), .in_8(undriven_80), .in_9(undriven_82), .in_10(undriven_84),
    .in_11(undriven_86), .in_12(undriven_88), .in_13(undriven_90), .in_14(undriven_92), .in_15(undriven_94),
    .in_16(undriven_96), .in_17(undriven_98), .in_18(undriven_100), .in_19(undriven_102),
    .in_20(undriven_104), .in_21(undriven_106), .in_22(undriven_108), .in_23(undriven_110),
    .in_24(undriven_112), .in_25(undriven_114), .in_26(undriven_116), .in_27(undriven_118),
    .in_28(undriven_120), .in_29(undriven_122), .in_30(undriven_124), .in_31(undriven_126),
    .in_32(undriven_128));  // open: sel, addr, data
  DotMatrix #(.matrixcols(32), .matrixrows(32)) dotmatrix_5 (
    .col0(undriven_129), .col1(undriven_131), .col2(undriven_133), .col3(undriven_135), .col4(undriven_137),
    .col5(undriven_139), .col6(undriven_141), .col7(undriven_143), .col8(undriven_145), .col9(undriven_147),
    .col10(undriven_149), .col11(undriven_151), .col12(undriven_153), .col13(undriven_155),
    .col14(undriven_157), .col15(undriven_159), .col16(undriven_161), .col17(undriven_163),
    .col18(undriven_165), .col19(undriven_167), .col20(undriven_169), .col21(undriven_171),
    .col22(undriven_173), .col23(undriven_175), .col24(undriven_177), .col25(undriven_179),
    .col26(undriven_181), .col27(undriven_183), .col28(undriven_185), .col29(undriven_187),
    .col30(undriven_189), .col31(undriven_191));
  DotMatrix #(.matrixcols(32), .matrixrows(32)) dotmatrix_6 (
    .col0(undriven_130), .col1(undriven_132), .col2(undriven_134), .col3(undriven_136), .col4(undriven_138),
    .col5(undriven_140), .col6(undriven_142), .col7(undriven_144), .col8(undriven_146), .col9(undriven_148),
    .col10(undriven_150), .col11(undriven_152), .col12(undriven_154), .col13(undriven_156),
    .col14(undriven_158), .col15(undriven_160), .col16(undriven_162), .col17(undriven_164),
    .col18(undriven_166), .col19(undriven_168), .col20(undriven_170), .col21(undriven_172),
    .col22(undriven_174), .col23(undriven_176), .col24(undriven_178), .col25(undriven_180),
    .col26(undriven_182), .col27(undriven_184), .col28(undriven_186), .col29(undriven_188),
    .col30(undriven_190), .col31(undriven_192));
  CPU cpu_1 (.WR(cpu_1_wr), .DI(mem_1_do), .ADR(cpu_1_adr), .DO(cpu_1_do));
  Screen_Control screen_control_5 (
    .in_1(undriven_129), .in_2(undriven_131), .in_3(undriven_133), .in_4(undriven_135), .in_5(undriven_137),
    .in_6(undriven_139), .in_7(undriven_141), .in_8(undriven_143), .in_9(undriven_145), .in_10(undriven_147),
    .in_11(undriven_149), .in_12(undriven_151), .in_13(undriven_153), .in_14(undriven_155),
    .in_15(undriven_157), .in_16(undriven_159), .in_17(undriven_161), .in_18(undriven_163),
    .in_19(undriven_165), .in_20(undriven_167), .in_21(undriven_169), .in_22(undriven_171),
    .in_23(undriven_173), .in_24(undriven_175), .in_25(undriven_177), .in_26(undriven_179),
    .in_27(undriven_181), .in_28(undriven_183), .in_29(undriven_185), .in_30(undriven_187),
    .in_31(undriven_189), .in_32(undriven_191));  // open: sel, addr, data
  Screen_Control screen_control_6 (
    .in_1(undriven_130), .in_2(undriven_132), .in_3(undriven_134), .in_4(undriven_136), .in_5(undriven_138),
    .in_6(undriven_140), .in_7(undriven_142), .in_8(undriven_144), .in_9(undriven_146), .in_10(undriven_148),
    .in_11(undriven_150), .in_12(undriven_152), .in_13(undriven_154), .in_14(undriven_156),
    .in_15(undriven_158), .in_16(undriven_160), .in_17(undriven_162), .in_18(undriven_164),
    .in_19(undriven_166), .in_20(undriven_168), .in_21(undriven_170), .in_22(undriven_172),
    .in_23(undriven_174), .in_24(undriven_176), .in_25(undriven_178), .in_26(undriven_180),
    .in_27(undriven_182), .in_28(undriven_184), .in_29(undriven_186), .in_30(undriven_188),
    .in_31(undriven_190), .in_32(undriven_192));  // open: sel, addr, data
  Mem mem_1 (.A(cpu_1_adr), .DO(mem_1_do), .DI(cpu_1_do), .WR(cpu_1_wr));
  DotMatrix #(.matrixcols(32), .matrixrows(32)) dotmatrix_7 (
    .col0(undriven_193), .col1(undriven_195), .col2(undriven_197), .col3(undriven_199), .col4(undriven_201),
    .col5(undriven_203), .col6(undriven_205), .col7(undriven_207), .col8(undriven_209), .col9(undriven_211),
    .col10(undriven_213), .col11(undriven_215), .col12(undriven_217), .col13(undriven_219),
    .col14(undriven_221), .col15(undriven_223), .col16(undriven_225), .col17(undriven_227),
    .col18(undriven_229), .col19(undriven_231), .col20(undriven_233), .col21(undriven_235),
    .col22(undriven_237), .col23(undriven_239), .col24(undriven_241), .col25(undriven_243),
    .col26(undriven_245), .col27(undriven_247), .col28(undriven_249), .col29(undriven_251),
    .col30(undriven_253), .col31(undriven_255));
  DotMatrix #(.matrixcols(32), .matrixrows(32)) dotmatrix_8 (
    .col0(undriven_194), .col1(undriven_196), .col2(undriven_198), .col3(undriven_200), .col4(undriven_202),
    .col5(undriven_204), .col6(undriven_206), .col7(undriven_208), .col8(undriven_210), .col9(undriven_212),
    .col10(undriven_214), .col11(undriven_216), .col12(undriven_218), .col13(undriven_220),
    .col14(undriven_222), .col15(undriven_224), .col16(undriven_226), .col17(undriven_228),
    .col18(undriven_230), .col19(undriven_232), .col20(undriven_234), .col21(undriven_236),
    .col22(undriven_238), .col23(undriven_240), .col24(undriven_242), .col25(undriven_244),
    .col26(undriven_246), .col27(undriven_248), .col28(undriven_250), .col29(undriven_252),
    .col30(undriven_254), .col31(undriven_256));
  Screen_Control screen_control_7 (
    .in_1(undriven_193), .in_2(undriven_195), .in_3(undriven_197), .in_4(undriven_199), .in_5(undriven_201),
    .in_6(undriven_203), .in_7(undriven_205), .in_8(undriven_207), .in_9(undriven_209), .in_10(undriven_211),
    .in_11(undriven_213), .in_12(undriven_215), .in_13(undriven_217), .in_14(undriven_219),
    .in_15(undriven_221), .in_16(undriven_223), .in_17(undriven_225), .in_18(undriven_227),
    .in_19(undriven_229), .in_20(undriven_231), .in_21(undriven_233), .in_22(undriven_235),
    .in_23(undriven_237), .in_24(undriven_239), .in_25(undriven_241), .in_26(undriven_243),
    .in_27(undriven_245), .in_28(undriven_247), .in_29(undriven_249), .in_30(undriven_251),
    .in_31(undriven_253), .in_32(undriven_255));  // open: sel, addr, data
  Screen_Control screen_control_8 (
    .in_1(undriven_194), .in_2(undriven_196), .in_3(undriven_198), .in_4(undriven_200), .in_5(undriven_202),
    .in_6(undriven_204), .in_7(undriven_206), .in_8(undriven_208), .in_9(undriven_210), .in_10(undriven_212),
    .in_11(undriven_214), .in_12(undriven_216), .in_13(undriven_218), .in_14(undriven_220),
    .in_15(undriven_222), .in_16(undriven_224), .in_17(undriven_226), .in_18(undriven_228),
    .in_19(undriven_230), .in_20(undriven_232), .in_21(undriven_234), .in_22(undriven_236),
    .in_23(undriven_238), .in_24(undriven_240), .in_25(undriven_242), .in_26(undriven_244),
    .in_27(undriven_246), .in_28(undriven_248), .in_29(undriven_250), .in_30(undriven_252),
    .in_31(undriven_254), .in_32(undriven_256));  // open: sel, addr, data
endmodule

module Chip_Tester (
  output [15:0] out_1
);

  wire NEXT_out, RESET_out;
  wire [5:0] rom_3_data;
  wire [7:0] counter_1_q;
  wire [15:0] alu_1_p9, rom_1_data, rom_2_data, rom_4_data;

  Counter counter_1 (.Q(counter_1_q), .clk(NEXT_out), .clr(RESET_out));  // open: load, D, count, carry
  Button NEXT (.out(NEXT_out));
  Button RESET (.out(RESET_out));
  ROM #(.dataWidth(16)) rom_1 (.addr(counter_1_q), .data(rom_1_data));  // open: sel
  ROM #(.dataWidth(16)) rom_2 (.addr(counter_1_q), .data(rom_2_data));  // open: sel
  ROM #(.dataWidth(6)) rom_3 (.addr(counter_1_q), .data(rom_3_data));  // open: sel
  ROM #(.dataWidth(16)) rom_4 (.addr(counter_1_q), .data(rom_4_data));  // open: sel
  // ALU alu_1: pin names not known; wires that end beside it: rom_1_data, rom_2_data, rom_3_data[5], rom_3_data[3], rom_3_data[4], rom_3_data[2], rom_3_data[1], rom_3_data[0], alu_1_p9
  assign out_1 = rom_4_data ^ alu_1_p9;  // XOR_Gate xor_1, 16 bits wide

  // Notes on the sheet:
  //   contents of rom_1 (hex, n*v repeats v):
  //   18*0 19*11
  //   contents of rom_2 (hex, n*v repeats v):
  //   18*ffff 18*3
  //   contents of rom_3 (hex, n*v repeats v):
  //   2a 3f 3a
endmodule

module CPU (
  input  [15:0] DI,
  output [15:0] ADR,
  output WR,
  output [15:0] DO
);

  wire alu_1_co, alu_1_ng, alu_1_zr, And16_out_2, and_1_out, and_2_out, and_3_out, CAR_q, clock_1_out,
       controlled_inverter_1_out, F0, F1, FD, flip_flop_1_out_4, J0, J1, J2, multiplexer_1_out, NG_q,
       not_1_out, PC_plus, pull_resistor_1_node, R0, R1, R2, RST, SD, UC, WA, WD, WP, WS, WX, ZR_q;
  wire [1:0] INS0_q_2;
  wire [2:0] SEL;
  wire [9:4] INS0_q;
  wire [15:0] A_q, controlled_buffer_1_out, controlled_buffer_2_out, D_q, INS1_q, multiplexer_2_out,
       multiplexer_3_out, multiplexer_4_out, PC_q, SP_q, undriven, X_q;

  Button button_1 (.out(RST));
  and and_1 (and_1_out, flip_flop_1_out_4, clock_1_out);
  Flip_flop flip_flop_1 (.in_1(RST), .in_2(And16_out_2), .out_4(flip_flop_1_out_4));  // open: out_3
  Clock clock_1 (.out(clock_1_out));
  Counter #(.width(3), .max('h7)) counter_1 (.Q(SEL), .clk(and_1_out), .clr(RST));  // open: load, D, count, carry
  Decoder #(.select(3), .disabled(0)) decoder_1 (
    .out0(SD), .out2(F0), .out4(F1), .out6(FD), .sel(SEL));  // open: out1, out3, out5, out7, en
  Register #(.width(1)) ZR (.D(alu_1_zr), .Q(ZR_q), .clk(SD), .clr(RST));  // open: en
  Register #(.width(1)) NG (.D(alu_1_ng), .Q(NG_q), .clk(SD), .clr(RST));  // open: en
  or or_1 (PC_plus, F0, F1);
  And16Way And16 (.in_1({R0, R1, R2, INS0_q_2, WP, INS0_q, UC, J0, J1, J2}), .out_2(And16_out_2));
  Pull_Resistor pull_resistor_1 (.node(pull_resistor_1_node));
  Register #(.width(16)) INS1 (.D(DI), .Q(INS1_q), .clk(F1), .clr(RST));  // open: en
  Register #(.width(16)) INS0 (
    .D(DI), .Q({R0, R1, R2, INS0_q_2, WP, INS0_q, UC, J0, J1, J2}), .clk(F0), .clr(RST));  // open: en
  Multiplexer #(.select(2)) multiplexer_1 (
    .in0(pull_resistor_1_node), .in1(ZR_q), .in2(NG_q), .in3(CAR_q), .out(multiplexer_1_out), .sel({J1, J0}));  // open: en
  Multiplexer #(.width(16)) multiplexer_2 (
    .in0(controlled_buffer_1_out), .in1(DI), .out(multiplexer_2_out), .sel(R2));  // open: en
  Decoder #(.select(2), .disabled(0)) decoder_2 (.out0(WA), .out1(WS), .out2(WX), .out3(WD), .sel(INS0_q_2), .en(SD));
  ALU alu_1 (
    .X(A_q), .OUT(DO), .CI(and_2_out), .ZX(INS0_q[9]), .ZY(INS0_q[7]), .NY(INS0_q[6]), .F(INS0_q[5]),
    .NO(INS0_q[4]), .Y(multiplexer_2_out), .NX(INS0_q[8]), .NG(alu_1_ng), .ZR(alu_1_zr), .CO(alu_1_co));
  and and_2 (and_2_out, CAR_q, UC);
  assign controlled_inverter_1_out = J2 ? ~multiplexer_1_out : 1'bz;  // Controlled_Inverter controlled_inverter_1
  Pull_Resistor pull_resistor_2 (.node(controlled_inverter_1_out));
  Register #(.width(16)) A (.D(DO), .Q(A_q), .clk(WA), .clr(RST));  // open: en
  Register #(.width(1)) CAR (.D(alu_1_co), .Q(CAR_q), .clk(SD), .clr(RST));  // open: en
  and and_3 (and_3_out, SD, controlled_inverter_1_out);
  Counter #(.width(16), .max('hffff), .trigger("falling")) PC (
    .load(and_3_out), .D(undriven), .Q(PC_q), .clk(PC_plus), .clr(RST));  // open: count, carry
  assign controlled_buffer_1_out = not_1_out ? multiplexer_3_out : 16'bz;  // Controlled_Buffer controlled_buffer_1
  not not_1 (not_1_out, R2);
  Register #(.width(16)) SP (.D(DO), .Q(SP_q), .clk(WS), .clr(RST));  // open: en
  Register #(.width(16)) X (.D(DO), .Q(X_q), .clk(WX), .clr(RST));  // open: en
  Register #(.width(16)) D (.D(DO), .Q(D_q), .clk(WD), .clr(RST));  // open: en
  assign controlled_buffer_2_out = R2 ? multiplexer_3_out : 16'bz;  // Controlled_Buffer controlled_buffer_2
  Multiplexer #(.select(2), .width(16)) multiplexer_3 (
    .in0(A_q), .in1(SP_q), .in2(X_q), .in3(D_q), .out(multiplexer_3_out), .sel({R0, R1}));  // open: en
  Multiplexer #(.select(2), .width(16)) multiplexer_4 (
    .in0(A_q), .in1(X_q), .in2(D_q), .in3(INS1_q), .out(multiplexer_4_out), .sel(INS0_q_2));  // open: en
  Multiplexer #(.select(2), .width(16)) multiplexer_5 (
    .in0(PC_q), .in1(PC_q), .in2(controlled_buffer_2_out), .in3(multiplexer_4_out), .out(ADR), .sel(SEL[2:1]));  // open: en
  Pull_Resistor pull_resistor_3 (.node(WR));

  // Notes on the sheet:
  //   Halt
  //   Jump Control
  //   Read Select
  //   Write Ptr Select
endmodule

module ALU (
  input  [15:0] X,
  input  ZX,
  input  NX,
  input  CI,
  input  [15:0] Y,
  input  ZY,
  input  NY,
  input  F,
  input  NO,
  output NG,
  output ZR,
  output [15:0] OUT,
  output CO
);

  wire adder_1_cout, not_1_out, not_2_out, not_3_out, Or16Way_out_2;
  wire [15:0] adder_1_out, and_1_out, multiplexer_1_out, n16and1_1_out_3, n16and1_2_out_3, n16xor1_1_out_3,
       n16xor1_2_out_3;

  not not_1 (not_1_out, ZX);
  not not_2 (not_2_out, ZY);
  _16And1 u_16and1_1 (.s(X), .out_3(n16and1_1_out_3), .a(not_1_out));
  _16And1 u_16and1_2 (.s(Y), .out_3(n16and1_2_out_3), .a(not_2_out));
  _16Xor1 u_16xor1_1 (.s(n16and1_1_out_3), .out_3(n16xor1_1_out_3), .a(NX));
  _16Xor1 u_16xor1_2 (.s(n16and1_2_out_3), .out_3(n16xor1_2_out_3), .a(NY));
  assign and_1_out = n16xor1_1_out_3 & n16xor1_2_out_3;  // AND_Gate and_1, 16 bits wide
  Adder #(.width(16)) adder_1 (
    .a(n16xor1_1_out_3), .b(n16xor1_2_out_3), .out(adder_1_out), .cin(CI), .cout(adder_1_cout));
  not not_3 (not_3_out, F);
  and and_2 (CO, adder_1_cout, not_3_out);
  Multiplexer #(.width(16)) multiplexer_1 (
    .in0(and_1_out), .in1(adder_1_out), .out(multiplexer_1_out), .sel(F));  // open: en
  _16Xor1 u_16xor1_3 (.s(multiplexer_1_out), .out_3({NG, OUT[14:0]}), .a(NO));
  not not_4 (ZR, Or16Way_out_2);
  Or16Way Or16Way (.in_1({NG, OUT[14:0]}), .out_2(Or16Way_out_2));

  assign OUT[15] = NG;
endmodule

module MemDev (
  input  [15:0] A,
  input  [15:0] DI,
  input  W,
  output [15:0] DO
);

  wire not_1_out, not_2_out, not_3_out;
  wire [15:0] multiplexer_1_out, ram_1_data;

  not not_1 (not_1_out, A[15]);
  Multiplexer #(.width(16)) multiplexer_1 (.out(multiplexer_1_out));  // open: in0, in1, sel, en
  RAM #(.addrWidth(15), .dataWidth(16), .bus("asynch")) ram_1 (
    .addr(A[14:0]), .data(ram_1_data), .sel(not_1_out), .ld(not_2_out));  // open: clr
  not not_2 (not_2_out, W);
  assign DO = A[15] ? multiplexer_1_out : 16'bz;  // Controlled_Buffer controlled_buffer_1
  not not_3 (not_3_out, A[15]);
  assign DO = not_3_out ? ram_1_data : 16'bz;  // Controlled_Buffer controlled_buffer_2
  assign ram_1_data = W ? DI : 16'bz;  // Controlled_Buffer controlled_buffer_3
endmodule

module Mem (
  input  [15:0] DI,
  input  [15:0] A,
  input  WR,
  output [15:0] DO
);

  wire not_1_out, not_2_out;
  wire [15:0] ram_1_data;

  RAM #(.addrWidth(16), .dataWidth(16)) ram_1 (
    .addr(A), .data(ram_1_data), .clk(WR), .ld(not_1_out));  // open: sel, clr
  not not_1 (not_1_out, WR);
  assign ram_1_data = WR ? DI : 16'bz;  // Controlled_Buffer controlled_buffer_1
  not not_2 (not_2_out, WR);
  assign DO = not_2_out ? ram_1_data : 16'bz;  // Controlled_Buffer controlled_buffer_2
endmodule

module Screen_Control (
  input  [31:0] in_1,
  input  [31:0] in_2,
  input  [31:0] in_3,
  input  [31:0] in_4,
  input  [31:0] in_5,
  input  [31:0] in_6,
  input  [31:0] in_7,
  input  [31:0] in_8,
  input  [31:0] in_9,
  input  [31:0] in_10,
  input  [31:0] in_11,
  input  [31:0] in_12,
  input  [31:0] in_13,
  input  [31:0] in_14,
  input  [31:0] in_15,
  input  [31:0] in_16,
  input  [31:0] in_17,
  input  [31:0] in_18,
  input  [31:0] in_19,
  input  [31:0] in_20,
  input  [31:0] in_21,
  input  [31:0] in_22,
  input  [31:0] in_23,
  input  [31:0] in_24,
  input  [31:0] in_25,
  input  [31:0] in_26,
  input  [31:0] in_27,
  input  [31:0] in_28,
  input  [31:0] in_29,
  input  [31:0] in_30,
  input  [31:0] in_31,
  input  [31:0] in_32,
  input  sel,
  input  addr,
  input  data
);
endmodule

module _16Xor1 (
  input  a,
  input  [15:0] s,
  output [15:0] out_3
);

  xor xor_1 (out_3[0], s[0], a);
  xor xor_2 (out_3[1], s[1], a);
  xor xor_3 (out_3[2], s[2], a);
  xor xor_4 (out_3[3], s[3], a);
  xor xor_5 (out_3[4], s[4], a);
  xor xor_6 (out_3[5], s[5], a);
  xor xor_7 (out_3[6], s[6], a);
  xor xor_8 (out_3[7], s[7], a);
  xor xor_9 (out_3[8], s[8], a);
  xor xor_10 (out_3[9], s[9], a);
  xor xor_11 (out_3[10], s[10], a);
  xor xor_12 (out_3[11], s[11], a);
  xor xor_13 (out_3[12], s[12], a);
  xor xor_14 (out_3[13], s[13], a);
  xor xor_15 (out_3[14], s[14], a);
  xor xor_16 (out_3[15], s[15], a);
endmodule

module _16And1 (
  input  a,
  input  [15:0] s,
  output [15:0] out_3
);

  and and_1 (out_3[0], s[0], a);
  and and_2 (out_3[1], s[1], a);
  and and_3 (out_3[2], s[2], a);
  and and_4 (out_3[3], s[3], a);
  and and_5 (out_3[4], s[4], a);
  and and_6 (out_3[5], s[5], a);
  and and_7 (out_3[6], s[6], a);
  and and_8 (out_3[7], s[7], a);
  and and_9 (out_3[8], s[8], a);
  and and_10 (out_3[9], s[9], a);
  and and_11 (out_3[10], s[10], a);
  and and_12 (out_3[11], s[11], a);
  and and_13 (out_3[12], s[12], a);
  and and_14 (out_3[13], s[13], a);
  and and_15 (out_3[14], s[14], a);
  and and_16 (out_3[15], s[15], a);
endmodule

module And16Way (
  input  [15:0] in_1,
  output out_2
);

  and and_1 (out_2, in_1[0], in_1[1], in_1[2], in_1[3], in_1[4], in_1[5], in_1[6], in_1[7], in_1[8], in_1[9], in_1[10], in_1[11], in_1[12], in_1[13], in_1[14], in_1[15]);
endmodule

module Or16Way (
  input  [15:0] in_1,
  output out_2
);

  or or_1 (out_2, in_1[0], in_1[1], in_1[2], in_1[3], in_1[4], in_1[5], in_1[6], in_1[7], in_1[8], in_1[9], in_1[10], in_1[11], in_1[12], in_1[13], in_1[14], in_1[15]);
endmodule

module Flip_flop (
  input  in_1,
  input  in_2,
  output out_3,
  output out_4
);

  nor nor_1 (out_3, in_1, out_4);
  nor nor_2 (out_4, out_3, in_2);
endmodule
